// Logisim project cpu.circ as structural Verilog: 4 circuits, main circuit main
module main (
  input  [31:0] INSTRUCTION,
  input  CLOCK,
  output [31:0] FETCH_ADDRESS,
  output [31:0] ra,
  output [31:0] sp,
  output [31:0] t0,
  output [31:0] t1,
  output [31:0] t2,
  output [31:0] s0,
  output [31:0] s1,
  output [31:0] a0
);

  wire ASel, brEQ, brLT, brUN, BSel, jump, memWE, PCsel, regWE;
  wire [1:0] WBSel;
  wire [3:0] ALUSel;
  wire [4:0] rd, rs1, rs2;
  wire [31:0] alu_result, DMEM_p5, immGen, multiplexer_1_out, multiplexer_2_out, multiplexer_3_out,
       multiplexer_4_out, multiplexer_5_out, pc, pc2, pc2add4, pcadd4, R1, R2, register_1_q;

  Adder #(.width(32)) adder_1 (.a(pc), .b(32'h4), .out(pcadd4));  // open: cin, cout
  Multiplexer #(.width(32), .enable("false")) multiplexer_1 (
    .in0(pcadd4), .in1(alu_result), .out(multiplexer_1_out), .sel(PCsel));
  // Probe on pcadd4
  // Probe on multiplexer_1_out
  Register #(.width(32)) register_1 (.D(multiplexer_2_out), .clk(CLOCK), .Q(register_1_q));  // open: en, clr
  Multiplexer #(.width(32), .enable("false")) multiplexer_2 (
    .in0(INSTRUCTION), .in1({32{1'b0}}), .out(multiplexer_2_out), .sel(jump));
  Shifter #(.width(32), .shift("lr")) shifter_1 (.in(pc), .\dist (5'b00010), .out(FETCH_ADDRESS));
  Register #(.width(32)) u_PC (.D(multiplexer_1_out), .clk(CLOCK), .Q(pc));  // open: en, clr
  // Probe on pc
  // Probe on alu_result
  Adder #(.width(32)) adder_2 (.a(pc2), .b(32'h4), .out(pc2add4));  // open: cin, cout
  // Probe on regWE
  // Probe on multiplexer_5_out
  control_unit control_unit_1 (
    .INSTRUCTION(register_1_q), .brEQ(brEQ), .brLT(brLT), .rs1(rs1), .rs2(rs2), .rd(rd), .brUN(brUN),
    .Asel(ASel), .PCsel(PCsel), .Bsel(BSel), .jump(jump), .ALUSel(ALUSel), .MEM_WE(memWE), .regWE(regWE),
    .WBsel(WBSel), .immediate(immGen));  // open: loadbyte, loadhalf, out_19
  // regfile_main RegFile: pin names not known; wires that end beside it: t0, t1, t2, s0, s1, a0, R1, R2
  // Probe on immGen
  Register #(.width(32)) register_2 (.D(pc), .clk(CLOCK), .Q(pc2));  // open: en, clr
  // Probe on pc2
  Multiplexer #(.width(32), .enable("false")) multiplexer_3 (
    .in0(R2), .in1(immGen), .out(multiplexer_3_out), .sel(BSel));
  // Probe on multiplexer_4_out
  Multiplexer #(.width(32), .enable("false")) multiplexer_4 (.in0(R1), .in1(pc2), .out(multiplexer_4_out), .sel(ASel));
  // Probe on t1
  // alu Arithmetic_Logic_Unit: pin names not known; wires that end beside it: multiplexer_4_out, multiplexer_3_out, ALUSel, alu_result
  // Probe on alu_result
  // Probe on alu_result
  branchcom branchcom_1 (.R1(R1), .R2(R2), .brUN(brUN), .brEQ(brEQ), .brLT(brLT));
  // Probe on immGen
  // Probe on pc2add4
  // mem_main DMEM: pin names not known; wires that end beside it: alu_result, R2, memWE, CLOCK, DMEM_p5
  // Probe on DMEM_p5
  Multiplexer #(.select(2), .width(32), .enable("false")) multiplexer_5 (
    .in0(pc2add4), .in1(alu_result), .in2(DMEM_p5), .out(multiplexer_5_out), .sel(WBSel));  // open: in3

  // Other names for the same wires on the sheet: clk = CLOCK; PROGRAM_COUNTER[31:0] = pc

  // Notes on the sheet:
  //   Output
  //   Inputs/Outputs from run.circ. DO NOT MOVE THESE.
  //   Inputs
  //   It is OK to move the PC, RegFile, ALU, and MEM to wherever is most convenient for you when constructing your CPU, and to delete this text
  //   Inputs/Outputs from run.circ. DO NOT MOVE THESE.
endmodule

module immGen1 (
  input  [24:0] Limm,
  input  [24:0] Simm,
  input  [24:0] SBimm,
  input  [24:0] Uimm,
  input  [2:0] ImmSel,
  input  [24:0] UJimm,
  output [31:0] ImmGen
);

  wire [31:0] bit_extender_1_out, bit_extender_2_out, bit_extender_3_out, bit_extender_4_out;

  assign bit_extender_1_out = {{20{Limm[24]}}, Limm[24:13]};  // Bit_Extender bit_extender_1
  assign bit_extender_2_out = {{20{Simm[24]}}, {Simm[24:18], Simm[4:0]}};  // Bit_Extender bit_extender_2
  assign bit_extender_3_out = {{19{SBimm[24]}}, {SBimm[24], SBimm[0], SBimm[23:18], SBimm[4:1], 1'b0}};  // Bit_Extender bit_extender_3
  assign bit_extender_4_out = {{11{UJimm[24]}}, {UJimm[24], UJimm[12:5], UJimm[13], UJimm[23:14], 1'b0}};  // Bit_Extender bit_extender_4
  Multiplexer #(.select(3), .width(32)) multiplexer_1 (
    .in0(bit_extender_1_out), .in1(bit_extender_2_out), .in2(bit_extender_3_out),
    .in3({Uimm[24:5], {12{1'b0}}}), .in4(bit_extender_4_out), .out(ImmGen), .sel(ImmSel));  // open: in5, in6, in7, en
endmodule

module branchcom (
  input  [31:0] R1,
  input  [31:0] R2,
  input  brUN,
  output brEQ,
  output brLT
);

  wire comparator_1_lt, comparator_2_lt;

  Comparator #(.width(32)) comparator_1 (.a(R1), .b(R2), .eq(brEQ), .lt(comparator_1_lt));  // open: gt
  Comparator #(.width(32), .mode("unsigned")) comparator_2 (.a(R1), .b(R2), .lt(comparator_2_lt));  // open: gt, eq
  Multiplexer #(.enable("false")) multiplexer_1 (.in0(comparator_1_lt), .in1(comparator_2_lt), .out(brLT), .sel(brUN));

  // Other names for the same wires on the sheet: A[31:0] = R1; B[31:0] = R2
endmodule

module control_unit (
  input  [31:0] INSTRUCTION,
  input  brEQ,
  input  brLT,
  output [4:0] rs1,
  output loadbyte,
  output [4:0] rs2,
  output loadhalf,
  output [4:0] rd,
  output brUN,
  output Asel,
  output PCsel,
  output Bsel,
  output jump,
  output [3:0] ALUSel,
  output MEM_WE,
  output regWE,
  output [1:0] WBsel,
  output [31:0] immediate,
  output out_19
);

  wire ADD_0, AND_1, and_1_out, and_2_out, and_3_out, and_4_out, and_43_out, and_44_out, and_45_out,
       and_46_out, BSEL_13, DIVU_8, f7_00, f7_01, f7_20, fun3_0, fun3_1, fun3_2, fun3_3, fun3_4, fun3_5,
       fun3_6, fun3_7, I03, I13, I67, i_addi, i_andi, i_jalr, i_lw, i_ori, i_slli, i_slti, i_srai, i_srli,
       i_xori, MULH_14, MULHU_11, MULT_10, or_1_out, OR_2, or_6_out, or_13_out, or_15_out, R, r_add, r_and,
       r_or, r_remu, r_sll, r_slt, r_srl, r_sub, r_xor, S, SB, sb_beq, sb_blt, sb_bne, SLL_6, SLT_7, SRL_4,
       UJ, XOR_3;
  wire [1:0] and_40_out, and_41_out, and_42_out, bit_extender_11_out, bit_extender_12_out,
       bit_extender_13_out;
  wire [3:0] and_47_out, and_48_out, and_49_out, and_50_out, and_51_out, and_52_out, and_53_out, and_54_out,
       and_55_out, and_56_out, and_57_out, and_58_out, and_59_out, and_60_out, and_61_out,
       bit_extender_14_out, bit_extender_15_out, bit_extender_16_out, bit_extender_17_out,
       bit_extender_18_out, bit_extender_19_out, bit_extender_20_out, bit_extender_21_out,
       bit_extender_22_out, bit_extender_23_out, bit_extender_24_out, bit_extender_25_out,
       bit_extender_26_out, bit_extender_27_out, bit_extender_28_out;
  wire [11:0] bit_extender_4_out, bit_extender_5_out;
  wire [19:0] bit_extender_3_out;
  wire [20:0] bit_extender_1_out, bit_extender_2_out;
  wire [31:0] and_19_out, and_20_out, and_21_out, and_22_out, and_23_out, bit_extender_6_out,
       bit_extender_7_out, bit_extender_8_out, bit_extender_9_out, bit_extender_10_out;

  assign bit_extender_1_out = {{20{INSTRUCTION[31]}}, INSTRUCTION[31]};  // Bit_Extender bit_extender_1
  assign bit_extender_2_out = {{20{INSTRUCTION[31]}}, INSTRUCTION[31]};  // Bit_Extender bit_extender_2
  assign bit_extender_3_out = {{19{INSTRUCTION[31]}}, INSTRUCTION[31]};  // Bit_Extender bit_extender_3
  assign bit_extender_4_out = {{11{INSTRUCTION[31]}}, INSTRUCTION[31]};  // Bit_Extender bit_extender_4
  assign bit_extender_5_out = {{11{1'b0}}, 1'b0};  // Bit_Extender bit_extender_5
  or or_1 (or_1_out, I03, I13, I67);
  and u_and_1 (and_1_out, sb_beq, brEQ);
  and and_2 (and_2_out, sb_blt, brLT);
  and and_3 (and_3_out, brUN, brLT);
  and and_4 (and_4_out, sb_bne, ~brEQ);  // AND_Gate
  or u_or_2 (regWE, I13, R, I03, I67, BSEL_13, UJ);
  and and_5 (r_add, R, fun3_0, f7_00);
  and and_6 (MULT_10, R, fun3_0, f7_01);
  and and_7 (r_sub, R, fun3_0, f7_20);
  and and_8 (r_sll, R, fun3_1, f7_00);
  and and_9 (MULH_14, R, fun3_1, f7_01);
  and and_10 (MULHU_11, R, fun3_3, f7_01);
  and and_11 (r_slt, R, fun3_2, f7_00);
  and and_12 (r_xor, R, fun3_4, f7_00);
  and and_13 (DIVU_8, R, fun3_5, f7_01);
  and and_14 (r_srl, R, fun3_5, f7_00);
  and and_15 (r_or, R, fun3_6, f7_00);
  and and_16 (r_remu, R, fun3_7, f7_01);
  and and_17 (r_and, R, fun3_7, f7_00);
  and and_18 (MEM_WE, S, fun3_2);
  assign bit_extender_6_out = {{31{or_1_out}}, or_1_out};  // Bit_Extender bit_extender_6
  assign bit_extender_7_out = {{31{S}}, S};  // Bit_Extender bit_extender_7
  assign bit_extender_8_out = {{31{SB}}, SB};  // Bit_Extender bit_extender_8
  assign bit_extender_9_out = {{31{BSEL_13}}, BSEL_13};  // Bit_Extender bit_extender_9
  assign bit_extender_10_out = {{31{UJ}}, UJ};  // Bit_Extender bit_extender_10
  // Probe on regWE
  assign and_19_out = {bit_extender_1_out, INSTRUCTION[30:20]} & bit_extender_6_out;  // AND_Gate and_19, 32 bits wide
  assign and_20_out = {bit_extender_2_out, INSTRUCTION[30:25], INSTRUCTION[11:7]} & bit_extender_7_out;  // AND_Gate and_20, 32 bits wide
  assign and_21_out = {bit_extender_3_out, INSTRUCTION[7], INSTRUCTION[30:25], INSTRUCTION[11:8], 1'b0} & bit_extender_8_out;  // AND_Gate and_21, 32 bits wide
  assign and_22_out = {INSTRUCTION[31:12], bit_extender_5_out} & bit_extender_9_out;  // AND_Gate and_22, 32 bits wide
  assign and_23_out = {bit_extender_4_out, INSTRUCTION[19:12], INSTRUCTION[20], INSTRUCTION[30:21], 1'b0} & bit_extender_10_out;  // AND_Gate and_23, 32 bits wide
  or or_3 (jump, UJ, i_jalr, and_1_out, and_2_out, and_3_out, and_4_out);
  Comparator #(.width(7)) comparator_1 (.a(INSTRUCTION[6:0]), .b(7'b0110011), .eq(R));  // open: gt, lt
  Comparator #(.width(7)) comparator_2 (.a(INSTRUCTION[6:0]), .b(7'b0000011), .eq(I03));  // open: gt, lt
  Comparator #(.width(7)) comparator_3 (.a(INSTRUCTION[6:0]), .b(7'b0010011), .eq(I13));  // open: gt, lt
  Comparator #(.width(7)) comparator_4 (.a(INSTRUCTION[6:0]), .b(7'b0100011), .eq(S));  // open: gt, lt
  Comparator #(.width(7)) comparator_5 (.a(INSTRUCTION[6:0]), .b(7'b1100011), .eq(SB));  // open: gt, lt
  Comparator #(.width(7)) comparator_6 (.a(INSTRUCTION[6:0]), .b(7'b0110111), .eq(BSEL_13));  // open: gt, lt
  Comparator #(.width(7)) comparator_7 (.a(INSTRUCTION[6:0]), .b(7'b1101111), .eq(UJ));  // open: gt, lt
  Comparator #(.width(7)) comparator_8 (.a(INSTRUCTION[6:0]), .b(7'b1100111), .eq(I67));  // open: gt, lt
  assign immediate = and_19_out | and_20_out | and_21_out | and_22_out | and_23_out;  // OR_Gate or_4, 32 bits wide
  // Probe on immediate
  Decoder #(.select(3), .enable("false")) decoder_1 (
    .out0(fun3_0), .out1(fun3_1), .out2(fun3_2), .out3(fun3_3), .out4(fun3_4), .out5(fun3_5), .out6(fun3_6),
    .out7(fun3_7), .sel(INSTRUCTION[14:12]));
  Decoder #(.select(3), .enable("false")) decoder_2 (
    .out0(fun3_0), .out1(fun3_1), .out2(fun3_2), .out3(fun3_3), .out4(fun3_4), .out5(fun3_5), .out6(fun3_6),
    .out7(fun3_7), .sel(INSTRUCTION[14:12]));
  and and_24 (loadbyte, I03, fun3_0);
  and and_25 (loadhalf, I03, fun3_1);
  and and_26 (i_lw, I03, fun3_2);
  and and_27 (i_addi, I13, fun3_0);
  and and_28 (i_slli, I13, fun3_1, f7_00);
  and and_29 (i_slti, I13, fun3_2);
  and and_30 (i_xori, I13, fun3_4);
  and and_31 (i_srli, I13, fun3_5, f7_00);
  and and_32 (i_srai, I13, fun3_5, f7_20);
  and and_33 (i_ori, I13, fun3_6);
  and and_34 (i_andi, I13, fun3_7);
  and and_35 (i_jalr, I67, fun3_0);
  and and_36 (sb_beq, SB, fun3_0);
  and and_37 (sb_blt, SB, fun3_4);
  and and_38 (brUN, SB, fun3_6);
  and and_39 (sb_bne, SB, fun3_1);
  Comparator #(.width(7)) comparator_9 (.a(INSTRUCTION[31:25]), .b({7{1'b0}}), .eq(f7_00));  // open: gt, lt
  Comparator #(.width(7)) comparator_10 (.a(INSTRUCTION[31:25]), .b(7'b0000001), .eq(f7_01));  // open: gt, lt
  Comparator #(.width(7)) comparator_11 (.a(INSTRUCTION[31:25]), .b(7'b0100000), .eq(f7_20));  // open: gt, lt
  or or_5 (ADD_0, r_add, loadbyte, loadhalf, i_lw, i_addi, MEM_WE, sb_beq, sb_blt, brUN, sb_bne, UJ, i_jalr);
  or or_6 (or_6_out, I67, UJ);
  or or_7 (AND_1, r_and, i_andi);
  or or_8 (OR_2, r_or, i_ori);
  or or_9 (XOR_3, r_xor, i_xori);
  or or_10 (SRL_4, r_srl, i_srli);
  or or_11 (SLL_6, r_sll, i_slli);
  or or_12 (SLT_7, i_slti, r_slt);
  assign bit_extender_11_out = {{1{or_13_out}}, or_13_out};  // Bit_Extender bit_extender_11
  or or_13 (or_13_out, I13, R, BSEL_13, out_19);
  assign bit_extender_12_out = {{1{I03}}, I03};  // Bit_Extender bit_extender_12
  assign bit_extender_13_out = {{1{or_6_out}}, or_6_out};  // Bit_Extender bit_extender_13
  Comparator #(.width(32)) comparator_12 (.a(INSTRUCTION), .b({32{1'b0}}), .eq(out_19));  // open: gt, lt
  assign and_40_out = bit_extender_11_out & 2'b01;  // AND_Gate and_40, 2 bits wide
  assign and_41_out = bit_extender_12_out & 2'b10;  // AND_Gate and_41, 2 bits wide
  assign and_42_out = bit_extender_13_out & 2'b00;  // AND_Gate and_42, 2 bits wide
  not not_1 (Bsel, R);
  not not_2 (Bsel, R);
  assign WBsel = and_40_out | and_41_out | and_42_out;  // OR_Gate or_14, 2 bits wide
  // Probe on WBsel
  or or_15 (or_15_out, R, I03, I13, S, I67);
  and and_43 (and_43_out, sb_beq, brEQ);
  and and_44 (and_44_out, sb_blt, brLT);
  and and_45 (and_45_out, brUN, brLT);
  and and_46 (and_46_out, sb_bne, ~brEQ);  // AND_Gate
  assign bit_extender_14_out = {{3{ADD_0}}, ADD_0};  // Bit_Extender bit_extender_14
  assign bit_extender_15_out = {{3{AND_1}}, AND_1};  // Bit_Extender bit_extender_15
  assign bit_extender_16_out = {{3{OR_2}}, OR_2};  // Bit_Extender bit_extender_16
  assign bit_extender_17_out = {{3{XOR_3}}, XOR_3};  // Bit_Extender bit_extender_17
  assign bit_extender_18_out = {{3{SRL_4}}, SRL_4};  // Bit_Extender bit_extender_18
  assign bit_extender_19_out = {{3{i_srai}}, i_srai};  // Bit_Extender bit_extender_19
  assign bit_extender_20_out = {{3{SLL_6}}, SLL_6};  // Bit_Extender bit_extender_20
  assign bit_extender_21_out = {{3{SLT_7}}, SLT_7};  // Bit_Extender bit_extender_21
  assign bit_extender_22_out = {{3{DIVU_8}}, DIVU_8};  // Bit_Extender bit_extender_22
  assign bit_extender_23_out = {{3{r_remu}}, r_remu};  // Bit_Extender bit_extender_23
  assign bit_extender_24_out = {{3{MULT_10}}, MULT_10};  // Bit_Extender bit_extender_24
  assign bit_extender_25_out = {{3{MULHU_11}}, MULHU_11};  // Bit_Extender bit_extender_25
  assign bit_extender_26_out = {{3{r_sub}}, r_sub};  // Bit_Extender bit_extender_26
  assign bit_extender_27_out = {{3{BSEL_13}}, BSEL_13};  // Bit_Extender bit_extender_27
  assign bit_extender_28_out = {{3{MULH_14}}, MULH_14};  // Bit_Extender bit_extender_28
  not not_3 (Asel, or_15_out);
  assign and_47_out = bit_extender_14_out & 4'b0000;  // AND_Gate and_47, 4 bits wide
  assign and_48_out = bit_extender_15_out & 4'b0001;  // AND_Gate and_48, 4 bits wide
  assign and_49_out = bit_extender_16_out & 4'b0010;  // AND_Gate and_49, 4 bits wide
  assign and_50_out = bit_extender_17_out & 4'b0011;  // AND_Gate and_50, 4 bits wide
  assign and_51_out = bit_extender_18_out & 4'b0100;  // AND_Gate and_51, 4 bits wide
  assign and_52_out = bit_extender_19_out & 4'b0101;  // AND_Gate and_52, 4 bits wide
  assign and_53_out = bit_extender_20_out & 4'b0110;  // AND_Gate and_53, 4 bits wide
  assign and_54_out = bit_extender_21_out & 4'b0111;  // AND_Gate and_54, 4 bits wide
  assign and_55_out = bit_extender_22_out & 4'b1000;  // AND_Gate and_55, 4 bits wide
  assign and_56_out = bit_extender_23_out & 4'b1001;  // AND_Gate and_56, 4 bits wide
  assign and_57_out = bit_extender_24_out & 4'b1010;  // AND_Gate and_57, 4 bits wide
  assign and_58_out = bit_extender_25_out & 4'b1011;  // AND_Gate and_58, 4 bits wide
  assign and_59_out = bit_extender_26_out & 4'b1100;  // AND_Gate and_59, 4 bits wide
  assign and_60_out = bit_extender_27_out & 4'b1101;  // AND_Gate and_60, 4 bits wide
  assign and_61_out = bit_extender_28_out & 4'b1110;  // AND_Gate and_61, 4 bits wide
  or or_16 (PCsel, and_43_out, and_44_out, and_45_out, and_46_out, UJ, i_jalr);
  assign ALUSel = and_47_out | and_48_out | and_49_out | and_50_out | and_51_out | and_52_out | and_53_out | and_54_out | and_55_out | and_56_out | and_57_out | and_58_out | and_59_out | and_60_out | and_61_out;  // OR_Gate or_17, 4 bits wide

  assign rd = INSTRUCTION[11:7];
  assign rs1 = INSTRUCTION[19:15];
  assign rs2 = INSTRUCTION[24:20];

  // Other names for the same wires on the sheet: ins_11_7[4:0] = INSTRUCTION[11:7]; ins_11_8[3:0] = INSTRUCTION[11:8];
  //   ins_7 = INSTRUCTION[7]; func7[6:0] = INSTRUCTION[31:25]; ins_31 = INSTRUCTION[31];
  //   ins_31_12[19:0] = INSTRUCTION[31:12]; ins_31_20[11:0] = INSTRUCTION[31:20]; func3[2:0] = INSTRUCTION[14:12];
  //   ins_19_12[7:0] = INSTRUCTION[19:12]; i_lb = loadbyte; i_lh = loadhalf; SRA_5 = i_srai; ins_20 = INSTRUCTION[20];
  //   ins_30_20[10:0] = INSTRUCTION[30:20]; ins_30_21[9:0] = INSTRUCTION[30:21]; ins_30_25[5:0] = INSTRUCTION[30:25];
  //   intype[6:0] = INSTRUCTION[6:0]; nop = out_19; PC_sel = PCsel; r_divu = DIVU_8; r_mul = MULT_10;
  //   r_mulh = MULH_14; r_mulhu = MULHU_11; REMU_9 = r_remu; SUB_12 = r_sub; s_sw = MEM_WE; sb_bltu = brUN;
  //   U = BSEL_13; u_lui = BSEL_13; uj_jal = UJ

  // Notes on the sheet:
  //   input
  //   split
  //   R_TYPE
  //   S_TYPE
  //   U_TYPE
  //   UJ_TYPE
  //   jump
  //   regWE
  //   OUTPUT
  //   type
  //   I_TYPE
  //   SB_TYPE
  //   ALU_SIGNAL
  //   WBsel
  //   0xFF1FF06F
  //   jal x0, func1
  //   0x00628463
  //   beq t0, t1, func2
  //   Asel
  //   Bsel
  //   PCsel
  //   brUN
endmodule
